// Logisim project BHDIK8.circ as structural Verilog: 9 circuits, main circuit main
module main (
);

  wire A_o, alu_1_a_larger, alu_1_carryout, alu_1_equal, alu_1_zero, and_1_out, and_2_out, and_3_out,
       and_4_out, and_5_out, and_6_out, C_o, clock_unit_1_clk, clock_unit_1_clke, clock_unit_1_clks, DA,
       demultiplexer_1_out1, demultiplexer_1_out2, demultiplexer_1_out3, E_ACC, E_BUS1, E_IAR, E_o, E_R0,
       E_R1, E_R2, E_R3, E_RAM, HLT, IO, IO_CLK_E, IO_CLK_S, not_1_out, not_2_out, not_3_out, S_ACC, S_FLAGS,
       S_IAR, S_IR, S_MAR, S_R0, S_R1, S_R2, S_R3, S_RAM, S_TMP, Z_o;
  wire [2:0] ALUOP;
  wire [3:0] XBUF_q, YBUF_q;
  wire [5:0] demultiplexer_1_out4;
  wire [6:0] keyboard_1_data, register_1_q;
  wire [7:0] alu_1_c, IAR_q, IOAddr_q, IR_q, MAR_q, multiplexer_1_out, ram_1_dout, rgb_video_1_p5_2, TMP_q;
  wire [15:0] rgb_video_1_p5;

  REGS IR (.S(S_IR), .D(IAR_q), .Q(IR_q));
  REGWS IAR (.D(IAR_q), .S(S_IAR), .E(E_IAR), .Q(IAR_q));
  CLOCK_UNIT clock_unit_1 (.HLT(HLT), .CLK(clock_unit_1_clk), .CLKE(clock_unit_1_clke), .CLKS(clock_unit_1_clks));
  CONTROL_UNIT control_unit_1 (
    .CLK(clock_unit_1_clk), .CLKE(clock_unit_1_clke), .CLKS(clock_unit_1_clks), .Z_f(Z_o), .E_f(E_o),
    .A_f(A_o), .C_f(C_o), .INSTRUCTION(IR_q), .E_RAM(E_RAM), .S_MAR(S_MAR), .E_ACC(E_ACC), .S_ACC(S_ACC),
    .E_R0(E_R0), .S_RAM(S_RAM), .E_R1(E_R1), .S_TMP(S_TMP), .E_R2(E_R2), .S_R0(S_R0), .E_R3(E_R3),
    .S_R1(S_R1), .E_IAR(E_IAR), .S_R2(S_R2), .E_BUS1(E_BUS1), .S_R3(S_R3), .IO_CLK_E(IO_CLK_E),
    .S_IAR(S_IAR), .ALUOP(ALUOP), .S_IR(S_IR), .S_FLAGS(S_FLAGS), .IO_CLK_S(IO_CLK_S), .HLT(HLT), .IO(IO),
    .DA(DA));
  FLAGS RFLAGS (
    .C_i(alu_1_carryout), .A_i(alu_1_a_larger), .E_i(alu_1_equal), .Z_i(alu_1_zero), .C_o(C_o), .A_o(A_o),
    .E_o(E_o), .Z_o(Z_o), .S(S_FLAGS));
  REGWS R0 (.D(IAR_q), .S(S_R0), .E(E_R0), .Q(IAR_q));
  and and_1 (and_1_out, DA, IO);
  REGWS R1 (.D(IAR_q), .S(S_R1), .E(E_R1), .Q(IAR_q));
  and and_2 (and_2_out, and_1_out, IO_CLK_S);
  not not_1 (not_1_out, DA);
  not not_2 (not_2_out, DA);
  not not_3 (not_3_out, IO);
  REGWS R2 (.D(IAR_q), .S(S_R2), .E(E_R2), .Q(IAR_q));
  ALU alu_1 (
    .CarryIN(1'b0), .OP(ALUOP), .A(IAR_q), .B(multiplexer_1_out), .CarryOut(alu_1_carryout), .C(alu_1_c),
    .Zero(alu_1_zero), .A_larger(alu_1_a_larger), .Equal(alu_1_equal));
  Multiplexer #(.width(8)) multiplexer_1 (.in0(TMP_q), .in1(8'h1), .out(multiplexer_1_out), .sel(E_BUS1));
  Register IOAddr (.D(IAR_q), .en(and_1_out), .clk(and_2_out), .Q(IOAddr_q));  // open: clr
  and and_3 (and_3_out, not_1_out, IO);
  and and_4 (and_4_out, not_2_out, not_3_out);
  REGWS R3 (.D(IAR_q), .S(S_R3), .E(E_R3), .Q(IAR_q));
  REGWS ACC (.D(alu_1_c), .S(S_ACC), .E(E_ACC), .Q(IAR_q));
  REGS TMP (.S(S_TMP), .D(IAR_q), .Q(TMP_q));
  and and_5 (and_5_out, and_3_out, IO_CLK_S);
  and and_6 (and_6_out, and_4_out, IO_CLK_E);
  Demultiplexer #(.select(4)) demultiplexer_1 (
    .out1(demultiplexer_1_out1), .out2(demultiplexer_1_out2), .out3(demultiplexer_1_out3),
    .out4(demultiplexer_1_out4[0]), .out5(demultiplexer_1_out4[1]), .out6(demultiplexer_1_out4[2]),
    .out7(demultiplexer_1_out4[3]), .out8(demultiplexer_1_out4[4]), .out9(demultiplexer_1_out4[5]),
    .in(1'b1), .sel(IOAddr_q[3:0]));  // open: out0, out10, out11, out12, out13, out14, out15
  RAM #(.trigger("high")) ram_1 (.addr(MAR_q), .we(S_RAM), .oe(E_RAM), .din(IAR_q), .dout(ram_1_dout));
  REGS MAR (.S(S_MAR), .D(IAR_q), .Q(MAR_q));
  TTY tty_1 (.data(IAR_q[6:0]), .clk(and_5_out), .we(demultiplexer_1_out1), .clr(demultiplexer_1_out2));
  Keyboard keyboard_1 (.clk(and_6_out), .re(demultiplexer_1_out3), .data(keyboard_1_data));  // open: clr, avail
  Register #(.trigger("high"), .width(4)) XBUF (
    .D(IAR_q[3:0]), .en(demultiplexer_1_out4[0]), .Q(XBUF_q), .clk(and_5_out));  // open: clr
  assign IAR_q = E_RAM ? ram_1_dout : 8'bz;  // Controlled_Buffer controlled_buffer_1
  Register #(.trigger("high"), .width(4)) YBUF (
    .D(IAR_q[3:0]), .en(demultiplexer_1_out4[1]), .Q(YBUF_q), .clk(and_5_out));  // open: clr
  Register #(.width(7)) register_1 (.D(keyboard_1_data), .Q(register_1_q), .clk(and_6_out));  // open: en, clr
  assign IAR_q = and_6_out ? {1'b0, register_1_q} : 8'bz;  // Controlled_Buffer controlled_buffer_2
  // RGB_Video #(.height(16), .scale(8), .width(16)) rgb_video_1: pin names not known; wires that end beside it: and_5_out, demultiplexer_1_out4[5], XBUF_q, YBUF_q, {rgb_video_1_p5_2, rgb_video_1_p5}, {rgb_video_1_p5_2, rgb_video_1_p5}
  Register #(.trigger("high")) BCBUF (
    .D(IAR_q), .en(demultiplexer_1_out4[2]), .Q(rgb_video_1_p5_2), .clk(and_5_out));  // open: clr
  Register #(.trigger("high")) GCBUF (
    .D(IAR_q), .en(demultiplexer_1_out4[3]), .Q(rgb_video_1_p5[15:8]), .clk(and_5_out));  // open: clr
  Register #(.trigger("high")) RCBUF (
    .D(IAR_q), .en(demultiplexer_1_out4[4]), .Q(rgb_video_1_p5[7:0]), .clk(and_5_out));  // open: clr

  // Notes on the sheet:
  //   BUS1
  //   I/O Controller
endmodule

module ALU (
  input  CarryIN,
  input  [2:0] OP,
  input  [7:0] A,
  input  [7:0] B,
  output CarryOut,
  output [7:0] C,
  output Zero,
  output A_larger,
  output Equal
);

  wire adder_1_cout;
  wire [7:0] adder_1_out, and_1_out, not_1_out, or_1_out, shifter_1_out, shifter_2_out, xor_1_out;

  Adder adder_1 (.a(A), .b(B), .out(adder_1_out), .cin(CarryIN), .cout(adder_1_cout));
  Shifter #(.shift("lr")) shifter_1 (.in(A), .\dist (3'b001), .out(shifter_1_out));
  Shifter shifter_2 (.in(A), .\dist (3'b001), .out(shifter_2_out));
  assign not_1_out = ~A;  // NOT_Gate not_1, 8 bits wide
  assign and_1_out = A & B;  // AND_Gate and_1, 8 bits wide
  assign or_1_out = A | B;  // OR_Gate or_1, 8 bits wide
  assign xor_1_out = A ^ B;  // XOR_Gate xor_1, 8 bits wide
  Comparator #(.mode("unsigned")) comparator_1 (.a(A), .b(B), .gt(A_larger), .eq(Equal));  // open: lt
  Multiplexer #(.select(3), .width(8)) multiplexer_1 (
    .in0(adder_1_out), .in1(shifter_1_out), .in2(shifter_2_out), .in3(not_1_out), .in4(and_1_out),
    .in5(or_1_out), .in6(xor_1_out), .in7(8'h1), .out(C), .sel(OP));
  Multiplexer #(.select(3)) multiplexer_2 (
    .in0(adder_1_cout), .in1(1'b0), .in2(1'b0), .in3(1'b0), .in4(1'b0), .in5(1'b0), .in6(1'b0), .in7(1'b0),
    .out(CarryOut), .sel(OP));
  is_zero is_zero_1 (.A(C), .out_zero(Zero));

  // Notes on the sheet:
  //   No carry out
  //   No carry out
  //   000 ADD
  //   001 SHR
  //   010 SHL
  //   011 NOT
  //   100 AND
  //   101 OR
  //   110 XOR
  //   111 COMP
endmodule

module is_zero (
  input  [7:0] A,
  output out_zero
);

  wire or_1_out;

  or or_1 (or_1_out, A[0], A[1], A[2], A[3], A[4], A[5], A[6], A[7]);
  not not_1 (out_zero, or_1_out);
endmodule

module STEPPER (
  input  RESET,
  input  CLK,
  output S1,
  output S2,
  output S3,
  output S4,
  output S5,
  output S6,
  output S7
);

  wire d_ff_1_q, d_ff_2_q, d_ff_3_q, d_ff_4_q, d_ff_5_q, d_ff_6_q, d_ff_7_q, d_ff_8_q, d_ff_9_q, d_ff_10_q,
       d_ff_11_q, not_1_out, not_2_out, not_3_out, not_4_out, not_5_out, not_6_out, not_7_out, not_8_out;

  not not_1 (not_1_out, RESET);
  not not_2 (not_2_out, CLK);
  D_Flip_Flop d_ff_1 (.D(not_1_out), .clk(not_2_out), .Q(d_ff_1_q), .reset(RESET));  // open: Qn, preset
  xor xor_1 (S1, RESET, not_3_out);
  not not_3 (not_3_out, d_ff_2_q);
  D_Flip_Flop d_ff_2 (.D(d_ff_1_q), .clk(CLK), .Q(d_ff_2_q), .reset(RESET));  // open: Qn, preset
  D_Flip_Flop d_ff_3 (.D(d_ff_2_q), .clk(not_2_out), .Q(d_ff_3_q), .reset(RESET));  // open: Qn, preset
  and and_1 (S2, d_ff_2_q, not_4_out);
  not not_4 (not_4_out, d_ff_4_q);
  D_Flip_Flop d_ff_4 (.D(d_ff_3_q), .clk(CLK), .Q(d_ff_4_q), .reset(RESET));  // open: Qn, preset
  D_Flip_Flop d_ff_5 (.D(d_ff_4_q), .clk(not_2_out), .Q(d_ff_5_q), .reset(RESET));  // open: Qn, preset
  and and_2 (S3, d_ff_4_q, not_5_out);
  not not_5 (not_5_out, d_ff_6_q);
  D_Flip_Flop d_ff_6 (.D(d_ff_5_q), .clk(CLK), .Q(d_ff_6_q), .reset(RESET));  // open: Qn, preset
  D_Flip_Flop d_ff_7 (.D(d_ff_6_q), .clk(not_2_out), .Q(d_ff_7_q), .reset(RESET));  // open: Qn, preset
  and and_3 (S4, d_ff_6_q, not_6_out);
  D_Flip_Flop d_ff_8 (.D(d_ff_7_q), .clk(CLK), .Q(d_ff_8_q), .reset(RESET));  // open: Qn, preset
  not not_6 (not_6_out, d_ff_8_q);
  and and_4 (S5, d_ff_8_q, not_7_out);
  D_Flip_Flop d_ff_9 (.D(d_ff_8_q), .clk(not_2_out), .Q(d_ff_9_q), .reset(RESET));  // open: Qn, preset
  not not_7 (not_7_out, d_ff_10_q);
  D_Flip_Flop d_ff_10 (.D(d_ff_9_q), .clk(CLK), .Q(d_ff_10_q), .reset(RESET));  // open: Qn, preset
  D_Flip_Flop d_ff_11 (.D(d_ff_10_q), .clk(not_2_out), .Q(d_ff_11_q), .reset(RESET));  // open: Qn, preset
  and and_5 (S6, d_ff_10_q, not_8_out);
  not not_8 (not_8_out, S7);
  D_Flip_Flop d_ff_12 (.D(d_ff_11_q), .clk(CLK), .Q(S7));  // open: Qn, preset, reset
endmodule

module CLOCK_UNIT (
  input  HLT,
  output CLK,
  output CLKE,
  output CLKS
);

  wire CLKD_i_out, CLKE_i_out, CLKS_i_out, not_1_out, t_ff_1_q;

  Clock #(.highDuration(2), .lowDuration(2), .phaseOffset(1)) CLK_i ();  // open: out
  Clock #(.highDuration(2), .lowDuration(2)) CLKD_i (.out(CLKD_i_out));
  Clock #(.highDuration(3)) CLKE_i (.out(CLKE_i_out));
  Clock #(.lowDuration(3), .phaseOffset(1)) CLKS_i (.out(CLKS_i_out));
  T_Flip_Flop t_ff_1 (.T(HLT), .clk(HLT), .Q(t_ff_1_q));  // open: Qn, reset, preset
  not not_1 (not_1_out, t_ff_1_q);
  and and_1 (CLK, CLKD_i_out, not_1_out);
  and and_2 (CLKE, CLKE_i_out, not_1_out);
  and and_3 (CLKS, CLKS_i_out, not_1_out);
endmodule

module CONTROL_UNIT (
  input  CLK,
  input  CLKE,
  input  CLKS,
  input  Z_f,
  input  E_f,
  input  A_f,
  input  C_f,
  input  [7:0] INSTRUCTION,
  output E_RAM,
  output S_MAR,
  output E_ACC,
  output S_ACC,
  output E_R0,
  output S_RAM,
  output E_R1,
  output S_TMP,
  output E_R2,
  output S_R0,
  output E_R3,
  output S_R1,
  output E_IAR,
  output S_R2,
  output E_BUS1,
  output S_R3,
  output IO_CLK_E,
  output S_IAR,
  output [2:0] ALUOP,
  output S_IR,
  output S_FLAGS,
  output IO_CLK_S,
  output HLT,
  output IO,
  output DA
);

  wire RESCYCLE;
  wire [2:0] STEP;
  wire [6:0] demultiplexer_1_out0, stepper_1_s1;
  wire [31:3] rom_1_data;

  and and_1 (E_RAM, rom_1_data[3], CLKE);
  and and_2 (E_ACC, rom_1_data[4], CLKE);
  and and_3 (E_R0, rom_1_data[5], CLKE);
  and and_4 (E_R1, rom_1_data[6], CLKE);
  and and_5 (E_R2, rom_1_data[7], CLKE);
  and and_6 (E_R3, rom_1_data[8], CLKE);
  and and_7 (E_IAR, rom_1_data[9], CLKE);
  and and_8 (E_BUS1, rom_1_data[10], CLKE);
  and and_9 (IO_CLK_E, rom_1_data[11], CLKE);
  ROM #(.addrWidth(16), .dataWidth(32)) rom_1 (
    .addr({INSTRUCTION, 1'b0, C_f, A_f, E_f, Z_f, STEP}),
    .data({rom_1_data[31:28], RESCYCLE, rom_1_data[26:3], ALUOP}));
  STEPPER stepper_1 (
    .RESET(stepper_1_s1[6]), .CLK(CLK), .S1(stepper_1_s1[0]), .S2(stepper_1_s1[1]), .S3(stepper_1_s1[2]),
    .S4(stepper_1_s1[3]), .S5(stepper_1_s1[4]), .S6(stepper_1_s1[5]), .S7(stepper_1_s1[6]));
  and and_10 (S_MAR, rom_1_data[12], CLKS);
  and and_11 (S_ACC, rom_1_data[13], CLKS);
  and and_12 (S_RAM, rom_1_data[14], CLKS);
  and and_13 (S_TMP, rom_1_data[15], CLKS);
  and and_14 (S_R0, rom_1_data[16], CLKS);
  and and_15 (S_R1, rom_1_data[17], CLKS);
  and and_16 (S_R2, rom_1_data[18], CLKS);
  and and_17 (S_R3, rom_1_data[19], CLKS);
  and and_18 (S_IAR, rom_1_data[20], CLKS);
  and and_19 (S_IR, rom_1_data[21], CLKS);
  and and_20 (S_FLAGS, rom_1_data[22], CLKS);
  and and_21 (IO_CLK_S, rom_1_data[23], CLKS);
  and and_22 (HLT, rom_1_data[24], CLKS);
  and and_23 (IO, rom_1_data[25], CLKE);
  and and_24 (DA, rom_1_data[26], CLKE);
  Counter #(.max('h6), .trigger("falling"), .width(3)) counter_1 (
    .clr(RESCYCLE), .clk(CLK), .Q(STEP));  // open: load, up, count, D, carry
  Demultiplexer #(.select(3)) demultiplexer_1 (
    .out0(demultiplexer_1_out0[0]), .out1(demultiplexer_1_out0[1]), .out2(demultiplexer_1_out0[2]),
    .out3(demultiplexer_1_out0[3]), .out4(demultiplexer_1_out0[4]), .out5(demultiplexer_1_out0[5]),
    .out6(demultiplexer_1_out0[6]), .in(1'b1), .sel(STEP));  // open: out7

  // Other names for the same wires on the sheet: FLAGS[3:0] = {C_f, A_f, E_f, Z_f}

  // Notes on the sheet:
  //   Conditional jump logic
  //   Enables
  //   T2 - enable RAM, set IR - read contents of memory location to IR
  //   contents of rom_1 (hex, n*v repeats v):
  //   3600 200008 100010 1020 10008 8000000 8000000 8000000 3600 200008 100010 1020 10008 8000000 8000000
  //   8000000 3600 200008 100010 1020 10008 8000000 8000000 8000000 3600 200008 100010 1020 10008 8000000
  //   8000000 8000000 3600 200008 100010 1020 10008 8000000 8000000 8000000 3600 200008 100010 1020 10008
  //   8000000 8000000 8000000 3600 200008 100010 1020 10008 8000000 8000000 8000000 3600 200008 100010
  //   1020 10008 8000000 8000000 8000000 3600 200008 100010 1020 10008 8000000 8000000 8000000 3600 200008
  //   100010 1020 10008 8000000 8000000 8000000 3600 200008 100010 1020 10008 8000000 8000000 8000000 3600
  //   200008 100010 1020 10008 8000000 8000000 8000000 3600 200008 100010 1020 10008 8000000 8000000
  //   8000000 3600 200008 100010 1020 10008 8000000 8000000 8000000 3600 200008 100010 1020 10008 8000000
  //   8000000 8000000 3600 200008 100010 1020 10008 8000000 8000000 8000000 3600 200008 100010 1020 10008
  //   8000000 8000000 8000000 3600 200008 100010 1020 10008 8000000 8000000 8000000 3600 200008 100010
  //   1020 10008 8000000 8000000 8000000 3600 200008 100010 1020 10008 8000000 8000000 8000000 3600 200008
  //   100010 1020 10008 8000000 8000000 8000000 3600 200008 100010 1020 10008 8000000 8000000 8000000 3600
  //   200008 100010 1020 10008 8000000 8000000 8000000 3600 200008 100010 1020 10008 8000000 8000000
  //   8000000 3600 200008 100010 1020 10008 8000000 8000000 8000000 3600 200008 100010 1020 10008 8000000
  //   8000000 8000000 3600 200008 100010 1020 10008 8000000 8000000 8000000 3600 200008 100010 1020 10008
  //   8000000 8000000 8000000 3600 200008 100010 1020 10008 8000000 8000000 8000000 3600 200008 100010
  //   1020 10008 8000000 8000000 8000000 3600 200008 100010 1020 10008 8000000 8000000 8000000 3600 200008
  //   100010 1020 10008 8000000 8000000 8000000 3600 200008 100010 1040 10008 8000000 8000000 8000000 3600
  //   200008 100010 1040 10008 8000000 8000000 8000000 3600 200008 100010 1040 10008 8000000 8000000
  //   8000000 3600 200008 100010 1040 10008 8000000 8000000 8000000 3600 200008 100010 1040 10008 8000000
  //   8000000 8000000 3600 200008 100010 1040 10008 8000000 8000000 8000000 3600 200008 100010 1040 10008
  //   8000000 8000000 8000000 3600 200008 100010 1040 10008 8000000 8000000 8000000 3600 200008 100010
  //   1040 10008 8000000 8000000 8000000 3600 200008 100010 1040 10008 8000000 8000000 8000000 3600 200008
  //   100010 1040 10008 8000000 8000000 8000000 3600 200008 100010 1040 10008 8000000 8000000 8000000 3600
  //   200008 100010 1040 10008 8000000 8000000 8000000 3600 200008 100010 1040 10008 8000000 8000000
  //   8000000 3600 200008 100010 1040 10008 8000000 8000000 8000000 3600 200008 100010 1040 10008 8000000
  //   8000000 8000000 3600 200008 100010 1040 10008 8000000 8000000 8000000 3600 200008 100010 1040 10008
  //   8000000 8000000 8000000 3600 200008 100010 1040 10008 8000000 8000000 8000000 3600 200008 100010
  //   1040 10008 8000000 8000000 8000000 3600 200008 100010 1040 10008 8000000 8000000 8000000 3600 200008
  //   100010 1040 10008 8000000 8000000 8000000 3600 200008 100010 1040 10008 8000000 8000000 8000000 3600
  //   200008 100010 1040 10008 8000000 8000000 8000000 3600 200008 100010 1040 10008 8000000 8000000
  //   8000000 3600 200008 100010 1040 10008 8000000 8000000 8000000 3600 200008 100010 1040 10008 8000000
  //   8000000 8000000 3600 200008 100010 1040 10008 8000000 8000000 8000000 3600 200008 100010 1040 10008
  //   8000000 8000000 8000000 3600 200008 100010 1040 10008 8000000 8000000 8000000 3600 200008 100010
  //   1040 10008 8000000 8000000 8000000 3600 200008 100010 1040 10008 8000000 8000000 8000000 3600 200008
  //   100010 1080 10008 8000000 8000000 8000000 3600 200008 100010 1080 10008 8000000 8000000 8000000 3600
  //   200008 100010 1080 10008 8000000 8000000 8000000 3600 200008 100010 1080 10008 8000000 8000000
  //   8000000 3600 200008 100010 1080 10008 8000000 8000000 8000000 3600 200008 100010 1080 10008 8000000
  //   8000000 8000000 3600 200008 100010 1080 10008 8000000 8000000 8000000 3600 200008 100010 1080 10008
  //   8000000 8000000 8000000 3600 200008 100010 1080 10008 8000000 8000000 8000000 3600 200008 100010
  //   1080 10008 8000000 8000000 8000000 3600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
  //   T3 - enable ACC, set IAR - get resulting sum IAR + 1 in ACC to IAR (increment IAR)
  //   T1 - enable IAR, enable BUS1, set ACC, set MAR - read content of IAR to get next instr. address and increment IAR
  //   Sets
endmodule

module REGWS (
  input  [7:0] D,
  input  S,
  input  E,
  output [7:0] Q
);

  wire [7:0] register_1_q;

  Register #(.trigger("high")) register_1 (.D(D), .en(S), .clk(S), .Q(register_1_q));  // open: clr
  assign Q = E ? register_1_q : 8'bz;  // Controlled_Buffer controlled_buffer_1
endmodule

module REGS (
  input  [7:0] D,
  input  S,
  output [7:0] Q
);

  REGWS TMP (.D(D), .S(S), .E(1'b1), .Q(Q));
endmodule

module FLAGS (
  input  C_i,
  input  A_i,
  input  E_i,
  input  Z_i,
  input  S,
  output C_o,
  output A_o,
  output E_o,
  output Z_o
);

  wire [7:4] regs_1_q;

  REGS regs_1 (.S(S), .D({4'b0000, Z_i, E_i, A_i, C_i}), .Q({regs_1_q, Z_o, E_o, A_o, C_o}));
endmodule
